// Logisim project CPU-addiu.circ as structural Verilog: 1 circuit, main circuit main
module main (
  output [31:0] t0,
  output [31:0] t1,
  output [31:0] t2,
  output [31:0] t3,
  output [23:0] Clock_Count,
  output halt
);

  wire mips_register_file_1_p1, RD_WRITE_ENABLE;
  wire [4:0] RD, RS, RT;
  wire [23:0] adder_1_out, FETCH_ADDRESS;
  wire [31:0] INSTRUCTION, RD_WRITE_VALUE, RS_READ_VALUE, RT_READ_VALUE;

  // Probe on FETCH_ADDRESS
  ROM #(.addrWidth(24), .dataWidth(32)) rom_1 (.addr(FETCH_ADDRESS), .data(INSTRUCTION));  // open: sel
  // Probe on INSTRUCTION
  // Probe on t0
  // MIPS_Register_File mips_register_file_1: pin names not known; wires that end beside it: mips_register_file_1_p1, RS_READ_VALUE, RT_READ_VALUE
  Clock clock_1 (.out(mips_register_file_1_p1));
  // Probe on t1
  cpu_main CPU (
    .RS_READ_VALUE(RS_READ_VALUE), .RT_READ_VALUE(RT_READ_VALUE), .INSTRUCTION(INSTRUCTION),
    .CLOCK(mips_register_file_1_p1), .RS(RS), .RT(RT), .Write_Register(RD), .RD_WRITE_VALUE(RD_WRITE_VALUE),
    .RD_WRITE_ENABLE(RD_WRITE_ENABLE), .FETCH_ADDRESS(FETCH_ADDRESS), .t0(t0), .t1(t1), .t2(t2), .t3(t3));  // open: RESET
  // Probe on t2
  Register #(.width(24)) register_1 (.D(adder_1_out), .Q(Clock_Count), .clk(mips_register_file_1_p1));  // open: en, clr
  // Probe on t3
  Adder #(.width(24)) adder_1 (.a(24'h1), .b(Clock_Count), .out(adder_1_out));  // open: cin, cout
  Comparator #(.width(24)) comparator_1 (.a(Clock_Count), .b(24'h6), .eq(halt));  // open: gt, lt

  // Notes on the sheet:
  //   contents of rom_1 (hex, n*v repeats v):
  //   25080022 2509002b 252affdd 250b0035 250a0062 2529002b 250a0064 250aff80
endmodule
