// Logisim project alu.circ as structural Verilog: 1 circuit, main circuit main
module main (
  input  [31:0] X,
  input  [31:0] Y,
  input  [5:0] Switch__S,
  output Signed_Overflow,
  output [31:0] RESULT,
  output Equal
);

  wire adder_1_cout, adder_2_cout, adder_4_cout, adder_5_cout, and_2_out, and_3_out, comparator_1_lt,
       comparator_2_eq, comparator_3_lt, not_1_out, not_2_out, not_3_out, not_4_out, not_5_out, or_2_out,
       subOverflow, sumOverflow;
  wire [31:0] ADD, ADDU, AND, BITPAL, multiplexer_1_out, multiplexer_2_out, negator_1_out, OR, SLL, SLT,
       SLTU, SRA, SRL, SUB, SUBU;
  wire [31:31] LFSR;

  Shifter #(.width(32)) shifter_1 (.in(X), .\dist (Y[4:0]), .out(SLL));
  Adder #(.width(31)) adder_1 (.a(X[30:0]), .b(Y[30:0]), .out(ADD[30:0]), .cout(adder_1_cout));  // open: cin
  Adder #(.width(1)) adder_2 (.a(Y[31]), .b(X[31]), .out(ADD[31]), .cin(adder_1_cout), .cout(adder_2_cout));
  assign AND = X & Y;  // AND_Gate and_1, 32 bits wide
  Comparator #(.width(32)) comparator_1 (.a(X), .b(Y), .lt(comparator_1_lt));  // open: gt, eq
  assign SLT = {{31{1'b0}}, comparator_1_lt};  // Bit_Extender bit_extender_1
  Comparator #(.width(16), .mode("unsigned")) comparator_2 (
    .a(X[31:16]), .b(X[15:0]), .eq(comparator_2_eq));  // open: gt, lt
  xor xor_1 (sumOverflow, adder_1_cout, adder_2_cout);
  assign BITPAL = {{31{1'b0}}, comparator_2_eq};  // Bit_Extender bit_extender_2
  Multiplexer #(.select(5), .width(32)) multiplexer_1 (
    .in0(SLL), .in2(SRL), .in3(SRA), .out(multiplexer_1_out), .sel(Switch__S[4:0]));  // open: in1, in4, in5, in6, in7, in8, in9, in10, in11, in12, in13, in14, in15, in16, in17, in18, in19, in20, in21, in22, in23, in24, in25, in26, in27, in28, in29, in30, in31, en
  Multiplexer #(.select(5), .width(32)) multiplexer_2 (
    .in0(ADD), .in1(ADDU), .in2(SUB), .in3(SUBU), .in4(AND), .in5(OR), .in10(SLT), .in11(SLTU),
    .in14(BITPAL), .in15({LFSR[31], X[31:1]}), .out(multiplexer_2_out), .sel(Switch__S[4:0]));  // open: in6, in7, in8, in9, in12, in13, in16, in17, in18, in19, in20, in21, in22, in23, in24, in25, in26, in27, in28, in29, in30, in31, en
  Multiplexer #(.width(32)) multiplexer_3 (
    .in0(multiplexer_1_out), .in1(multiplexer_2_out), .out(RESULT), .sel(Switch__S[5]));  // open: en
  Shifter #(.width(32), .shift("ar")) shifter_2 (.in(X), .\dist (Y[4:0]), .out(SRA));
  Adder #(.width(32)) adder_3 (.a(X), .b(Y), .out(ADDU));  // open: cin, cout
  assign OR = X | Y;  // OR_Gate or_1, 32 bits wide
  Comparator #(.width(32), .mode("unsigned")) comparator_3 (.a(X), .b(Y), .lt(comparator_3_lt));  // open: gt, eq
  assign SLTU = {{31{1'b0}}, comparator_3_lt};  // Bit_Extender bit_extender_3
  ExactlyOne xor_2 (.out(LFSR[31]), .in0(X[0]), .in1(X[2]), .in2(X[3]), .in3(X[5]));
  not not_1 (not_1_out, Switch__S[1]);
  Negator #(.width(32)) negator_1 (.in(Y), .out(negator_1_out));
  Comparator #(.width(32)) comparator_4 (.a(X), .b(Y), .eq(Equal));  // open: gt, lt
  and and_2 (and_2_out, sumOverflow, Switch__S[1]);
  and and_3 (and_3_out, not_1_out, subOverflow);
  Shifter #(.width(32), .shift("lr")) shifter_3 (.in(X), .\dist (Y[4:0]), .out(SRL));
  or or_2 (or_2_out, and_2_out, and_3_out);
  Adder #(.width(31)) adder_4 (
    .a(X[30:0]), .b(negator_1_out[30:0]), .out(SUB[30:0]), .cout(adder_4_cout));  // open: cin
  Adder #(.width(1)) adder_5 (.a(negator_1_out[31]), .b(X[31]), .out(SUB[31]), .cin(adder_4_cout), .cout(adder_5_cout));
  xor xor_3 (subOverflow, adder_4_cout, adder_5_cout);
  not not_2 (not_2_out, Switch__S[0]);
  not not_3 (not_3_out, Switch__S[2]);
  not not_4 (not_4_out, Switch__S[3]);
  and and_4 (Signed_Overflow, or_2_out, not_2_out, not_3_out, not_5_out, Switch__S[5]);
  not not_5 (not_5_out, Switch__S[4]);
  Subtractor #(.width(32)) subtractor_1 (.a(X), .b(Y), .out(SUBU));  // open: bin, bout

  // Other names for the same wires on the sheet: INPUT_X[31:0] = X; INPUT_Y[31:0] = Y; LFSR[30:0] = X[31:1]

  // Notes on the sheet:
  //   INPUTS to your circuit
  //   INPUT to your circuit
  //   DON'T CHANGE THE INPUTS AND OUTPUTS! IF YOU DO SO, YOU NEED TO MAKE SURE THE PINS ARE IN THE RIGHT PLACES!
  //   OUTPUTS of your circuit
endmodule
