// Logisim project cpu.circ as structural Verilog: 3 circuits, main circuit main
module main (
  input  [31:0] RS_READ_VALUE,
  input  [31:0] RT_READ_VALUE,
  input  [31:0] INSTRUCTION,
  input  CLOCK,
  input  RESET,
  output [31:0] t0,
  output [31:0] t1,
  output [31:0] t2,
  output [31:0] t3,
  output [4:0] RS,
  output [4:0] RT,
  output [4:0] Write_Register,
  output [31:0] RD_WRITE_VALUE,
  output RD_WRITE_ENABLE,
  output [23:0] FETCH_ADDRESS
);

  wire ALU_signed_overflow, and_1_out, BRANCH, bubble, ByteSigned, EQUAL, INM, InmSign,
       ist0_t4_1_to_instr_mem, ist0_t4_2_to_instr_mem, ist0_t4_3_to_instr_mem, JAL, JR, JUMP, MemByte,
       not_1_out, not_2_out, or_1_out, RegDst, SHIFT, WRITE_MEM, WRITE_REG;
  wire [1:0] WriteSrc;
  wire [4:0] multiplexer_1_out, rd;
  wire [5:0] ALUOp, funct, opcode;
  wire [23:0] adder_1_out, adder_2_out, adder_3_out, bit_extender_1_out, JumpAddr, multiplexer_4_out,
       multiplexer_7_out, multiplexer_8_out, multiplexer_13_out;
  wire [26:22] PC_q;
  wire [31:0] ALU_result, bit_extender_2_out, bit_extender_3_out, bit_extender_4_out, bit_extender_5_out,
       MEM_data_mem_out, multiplexer_3_out, multiplexer_9_out, multiplexer_10_out, multiplexer_11_out,
       multiplexer_12_out, RegFile_read_data_1, RegFile_read_data_2, RS_VALUE, RT_VALUE;
  wire [31:24] bit_extender_1_out_2;

  Multiplexer #(.width(5)) multiplexer_1 (.in0(RT), .in1(rd), .out(multiplexer_1_out), .sel(RegDst));  // open: en
  isT0_T4 ist0_t4_1 (.in_1(RT[4:2]), .To_Instr_Mem(ist0_t4_1_to_instr_mem));
  Multiplexer #(.width(5)) multiplexer_2 (
    .in0(multiplexer_1_out), .in1({5{1'b1}}), .out(Write_Register), .sel(JAL));  // open: en
  isT0_T4 ist0_t4_2 (.in_1(RS[4:2]), .To_Instr_Mem(ist0_t4_2_to_instr_mem));
  isT0_T4 ist0_t4_3 (.in_1(Write_Register[4:2]), .To_Instr_Mem(ist0_t4_3_to_instr_mem));
  regfile_main RegFile (
    .Read_register_1(RS[1:0]), .Read_register_2(RT[1:0]), .write_register(Write_Register[1:0]),
    .write_data(RD_WRITE_VALUE), .t0_Value(t0), .t1_Value(t1), .t2_Value(t2), .t3_Value(t3),
    .RegWrite(and_1_out), .clock(CLOCK), .Read_Data_1(RegFile_read_data_1), .Read_Data_2(RegFile_read_data_2));
  and and_1 (and_1_out, WRITE_REG, ist0_t4_3_to_instr_mem);
  not not_1 (not_1_out, ist0_t4_3_to_instr_mem);
  Adder #(.width(24)) adder_1 (.a(FETCH_ADDRESS), .b(24'h1), .out(adder_1_out));  // open: cin, cout
  Adder #(.width(24)) adder_2 (.a(FETCH_ADDRESS), .b(bit_extender_1_out), .out(adder_2_out));  // open: cin, cout
  and and_2 (RD_WRITE_ENABLE, WRITE_REG, not_1_out);
  Multiplexer #(.width(32)) multiplexer_3 (
    .in0(INSTRUCTION), .in1({32{1'b0}}), .out(multiplexer_3_out), .sel(bubble));  // open: en
  Multiplexer #(.width(24)) multiplexer_4 (
    .in0(adder_1_out), .in1(adder_2_out), .out(multiplexer_4_out), .sel(BRANCH));  // open: en
  Multiplexer #(.width(32)) multiplexer_5 (
    .in0(RS_READ_VALUE), .in1(RegFile_read_data_1), .out(RS_VALUE), .sel(ist0_t4_2_to_instr_mem));  // open: en
  Multiplexer #(.width(32)) multiplexer_6 (
    .in0(RT_READ_VALUE), .in1(RegFile_read_data_2), .out(RT_VALUE), .sel(ist0_t4_1_to_instr_mem));  // open: en
  Multiplexer #(.width(24)) multiplexer_7 (
    .in0(multiplexer_4_out), .in1(JumpAddr), .out(multiplexer_7_out), .sel(JUMP));  // open: en
  Register #(.width(32)) PC (
    .D(multiplexer_3_out), .Q({opcode, RS, RT, rd, PC_q, funct}), .clk(CLOCK));  // open: en, clr
  Multiplexer #(.width(24)) multiplexer_8 (
    .in0({RS[2:0], RT, rd, PC_q, funct}), .in1(RS_VALUE[23:0]), .out(multiplexer_8_out), .sel(JR));  // open: en
  assign {bit_extender_1_out_2, bit_extender_1_out} = {{16{rd[4]}}, {rd, PC_q, funct}};  // Bit_Extender bit_extender_1
  Register #(.width(24)) PC_2 (.D(multiplexer_7_out), .Q(FETCH_ADDRESS), .clk(CLOCK));  // open: en, clr
  assign bit_extender_2_out = {{27{1'b0}}, PC_q};  // Bit_Extender bit_extender_2
  assign bit_extender_3_out = {{16{1'b0}}, {rd, PC_q, funct}};  // Bit_Extender bit_extender_3
  Subtractor #(.width(24)) subtractor_1 (.a(multiplexer_8_out), .b(24'h100000), .out(JumpAddr));  // open: bin, bout
  Multiplexer #(.width(32)) multiplexer_9 (
    .in0(RT_VALUE), .in1(multiplexer_10_out), .out(multiplexer_9_out), .sel(INM));  // open: en
  Multiplexer #(.width(32)) multiplexer_10 (
    .in0(bit_extender_3_out), .in1({bit_extender_1_out_2, bit_extender_1_out}), .out(multiplexer_10_out),
    .sel(InmSign));  // open: en
  or or_1 (or_1_out, funct[0], funct[1], funct[2], funct[3], funct[4], funct[5], PC_q[22], PC_q[23], PC_q[24], PC_q[25], PC_q[26], rd[0], rd[1], rd[2], rd[3], rd[4], RT[1], RT[2], RT[3], RT[4], RS[0], RS[1], RS[2], RS[3], RS[4], opcode[0], opcode[1], opcode[2], opcode[3], opcode[4], opcode[5], RT[0]);
  not not_2 (not_2_out, or_1_out);
  Multiplexer #(.width(32)) multiplexer_11 (
    .in0(RS_VALUE), .in1(RT_VALUE), .out(multiplexer_11_out), .sel(SHIFT));  // open: en
  Multiplexer #(.width(32)) multiplexer_12 (
    .in0(multiplexer_9_out), .in1(bit_extender_2_out), .out(multiplexer_12_out), .sel(SHIFT));  // open: en
  CONTROLLER controller_1 (
    .OPCODE(opcode), .FUNCT(funct), .EQUAL(EQUAL), .NOP(not_2_out), .BRANCH(BRANCH), .JUMP(JUMP),
    .bubble(bubble), .JR(JR), .InmSign(InmSign), .INM(INM), .SHIFT(SHIFT), .ALUOp(ALUOp),
    .WRITE_MEM(WRITE_MEM), .ByteSigned(ByteSigned), .WriteSrc(WriteSrc), .JAL(JAL), .WRITE_REG(WRITE_REG),
    .RegDst(RegDst));
  alu_main ALU (
    .Switch__S(ALUOp), .X(multiplexer_11_out), .Equal(EQUAL), .RESULT(ALU_result),
    .Signed_Overflow(ALU_signed_overflow), .Y(multiplexer_12_out));
  LED led_1 (.in(ALU_signed_overflow));
  // Probe on multiplexer_11_out
  // Probe on multiplexer_12_out
  mem_main MEM (
    .Data_Mem_Addr(ALU_result), .Data_Mem_In(RT_VALUE), .ACCESS_BYTE(MemByte), .MEM_WRITE(WRITE_MEM),
    .CLOCK(CLOCK), .Data_Mem_Out(MEM_data_mem_out));
  // Probe on ALUOp
  assign bit_extender_4_out = {{24{MEM_data_mem_out[7]}}, MEM_data_mem_out[7:0]};  // Bit_Extender bit_extender_4
  Multiplexer #(.width(24)) multiplexer_13 (
    .in0(MEM_data_mem_out[31:8]), .in1(bit_extender_4_out[31:8]), .out(multiplexer_13_out), .sel(ByteSigned));  // open: en
  Adder #(.width(24)) adder_3 (.a(FETCH_ADDRESS), .b(24'h100000), .out(adder_3_out));  // open: cin, cout
  assign bit_extender_5_out = {{8{1'b0}}, adder_3_out};  // Bit_Extender bit_extender_5
  // Probe on RD_WRITE_VALUE
  Multiplexer #(.select(2), .width(32)) multiplexer_14 (
    .in0(ALU_result), .in1({multiplexer_13_out, MEM_data_mem_out[7:0]}), .in2({rd, PC_q, funct, {16{1'b0}}}),
    .in3(bit_extender_5_out), .out(RD_WRITE_VALUE), .sel(WriteSrc));  // open: en
  // Probe on WriteSrc

  // Other names for the same wires on the sheet: CLK = CLOCK; FETCH_I[23:0] = FETCH_ADDRESS; INST[31:0] = INSTRUCTION;
  //   WRITE_FLAG = RD_WRITE_ENABLE; WRITE_VALUE[31:0] = RD_WRITE_VALUE

  // Notes on the sheet:
  //   These are outputs/inputs from run.circ
  //   These are outputs to run.circ
  //   Feel free to move these components
endmodule

module isT0_T4 (
  input  [2:0] in_1,
  output To_Instr_Mem
);

  wire not_1_out, not_2_out;

  not not_1 (not_1_out, in_1[0]);
  and and_1 (To_Instr_Mem, not_1_out, in_1[1], not_2_out);
  not not_2 (not_2_out, in_1[2]);
endmodule

module CONTROLLER (
  input  [5:0] OPCODE,
  input  [5:0] FUNCT,
  input  EQUAL,
  input  NOP,
  output BRANCH,
  output JUMP,
  output bubble,
  output JR,
  output InmSign,
  output INM,
  output SHIFT,
  output [5:0] ALUOp,
  output WRITE_MEM,
  output ByteSigned,
  output [1:0] WriteSrc,
  output JAL,
  output WRITE_REG,
  output RegDst
);

  wire add, addiu, addu, \and , and_2_out, and_3_out, and_4_out, and_5_out, and_6_out, and_7_out, and_8_out,
       and_9_out, and_10_out, and_14_out, and_15_out, and_16_out, and_30_out, and_31_out, and_36_out,
       and_39_out, andi, beq, bitpal, bne, j, lbu, lfsr, lui, lw, not_2_out, not_3_out, not_4_out, not_5_out,
       not_6_out, not_7_out, not_8_out, not_9_out, not_10_out, not_11_out, not_12_out, not_13_out,
       not_14_out, NOT_NOP, \or , or_3_out, or_5_out, ori, R_TYPE, sll, slt, sltu, sra, srl, sub, subu;
  wire [2:0] or_9_out;

  not not_1 (NOT_NOP, NOP);
  not not_2 (not_2_out, OPCODE[5]);
  not not_3 (not_3_out, OPCODE[4]);
  not not_4 (not_4_out, OPCODE[3]);
  not not_5 (not_5_out, OPCODE[2]);
  not not_6 (not_6_out, OPCODE[1]);
  not not_7 (not_7_out, OPCODE[0]);
  not not_8 (not_8_out, FUNCT[5]);
  not not_9 (not_9_out, FUNCT[4]);
  not not_10 (not_10_out, FUNCT[3]);
  not not_11 (not_11_out, FUNCT[2]);
  not not_12 (not_12_out, FUNCT[1]);
  not not_13 (not_13_out, FUNCT[0]);
  not not_14 (not_14_out, EQUAL);
  or or_1 (JUMP, JR, j, JAL);
  and and_1 (R_TYPE, not_7_out, not_6_out, not_5_out, not_4_out, not_3_out, not_2_out);
  and and_2 (and_2_out, EQUAL, beq);
  and and_3 (and_3_out, not_14_out, bne);
  and and_4 (and_4_out, R_TYPE, not_9_out);
  or or_2 (BRANCH, and_2_out, and_3_out);
  and and_5 (and_5_out, not_2_out, not_3_out);
  and and_6 (and_6_out, OPCODE[5], not_3_out);
  and and_7 (and_7_out, not_11_out, not_10_out, not_8_out, and_4_out);
  and and_8 (and_8_out, not_4_out, and_5_out);
  and and_9 (and_9_out, OPCODE[3], and_5_out);
  and and_10 (and_10_out, FUNCT[5], and_4_out);
  and and_11 (sll, and_7_out, not_12_out, not_13_out);
  and and_12 (srl, and_7_out, not_13_out, FUNCT[1]);
  and and_13 (sra, and_7_out, FUNCT[1], FUNCT[0]);
  or or_3 (or_3_out, andi, lw, addiu, ByteSigned, lbu);
  and and_14 (and_14_out, OPCODE[2], not_6_out, and_8_out);
  and and_15 (and_15_out, not_5_out, OPCODE[1], and_8_out);
  and and_16 (and_16_out, not_11_out, not_10_out, and_10_out);
  or or_4 (bubble, BRANCH, JUMP);
  or or_5 (or_5_out, or_3_out, WRITE_MEM);
  and and_17 (beq, not_7_out, and_14_out);
  and and_18 (bne, OPCODE[0], and_14_out);
  and and_19 (JAL, not_7_out, and_15_out);
  and and_20 (j, OPCODE[0], and_15_out);
  and and_21 (add, and_16_out, not_12_out, not_13_out);
  and and_22 (addu, and_16_out, not_12_out, FUNCT[0]);
  and and_23 (sub, and_16_out, FUNCT[1], not_13_out);
  and and_24 (subu, and_16_out, FUNCT[1], FUNCT[0]);
  or or_6 (InmSign, beq, bne, or_5_out);
  or or_7 (INM, or_5_out, ori);
  or or_8 (or_9_out[2], andi, ori);
  or or_9 (or_9_out[0], ori, addiu);
  and and_25 (RegDst, R_TYPE, NOT_NOP);
  and and_26 (addiu, not_5_out, not_6_out, OPCODE[0], and_9_out);
  and and_27 (andi, OPCODE[2], not_6_out, not_7_out, and_9_out);
  and and_28 (ori, OPCODE[2], not_6_out, OPCODE[0], and_9_out);
  and and_29 (lui, OPCODE[2], OPCODE[1], OPCODE[0], and_9_out);
  or or_10 (SHIFT, sll, srl, sra);
  Multiplexer #(.width(6)) multiplexer_1 (
    .in0({3'b100, or_9_out[2], 1'b0, or_9_out[0]}), .in1(FUNCT), .out(ALUOp), .sel(R_TYPE));  // open: en
  or or_11 (WriteSrc[0], ByteSigned, lbu, lw, JAL);
  or or_12 (WriteSrc[1], JAL, lui);
  or or_13 (WRITE_REG, RegDst, or_3_out, ori, lui);
  and and_30 (and_30_out, not_10_out, FUNCT[2], not_12_out, and_10_out);
  and and_31 (and_31_out, FUNCT[3], not_11_out, FUNCT[1], and_10_out);
  and and_32 (\and , not_13_out, and_30_out);
  and and_33 (\or , FUNCT[0], and_30_out);
  and and_34 (slt, not_13_out, and_31_out);
  and and_35 (sltu, FUNCT[0], and_31_out);
  and and_36 (and_36_out, OPCODE[0], OPCODE[1], not_5_out, and_6_out);
  and and_37 (lw, not_4_out, and_36_out);
  and and_38 (WRITE_MEM, OPCODE[3], and_36_out);
  and and_39 (and_39_out, FUNCT[1], FUNCT[2], FUNCT[3], FUNCT[4], R_TYPE, FUNCT[5]);
  and and_40 (bitpal, not_13_out, and_39_out);
  and and_41 (lfsr, FUNCT[0], and_39_out);
  and and_42 (ByteSigned, not_7_out, not_6_out, not_5_out, not_4_out, and_6_out);
  and and_43 (lbu, not_7_out, not_6_out, not_4_out, OPCODE[2], and_6_out);
  and and_44 (JR, not_8_out, not_9_out, FUNCT[3], not_12_out, not_13_out, R_TYPE);

  // Other names for the same wires on the sheet: fun[5:0] = FUNCT; lb = ByteSigned; sw = WRITE_MEM
endmodule
